# Fritzing sketch pinout (saved by Fritzing 0.9.3b)

parts:
  S1 = Round Pushbutton
  MCU1 = Raspberry Pi Zero

nets:
  N1: S1.leg0, MCU1.pin_5
  N2: S1.leg1, MCU1.pin_6, MCU1.pin_34

notes:
  Pin 5 (SCL)
  Pin 6 (GND)
